# Fritzing sketch DP S01 (saved by Fritzing 0.9.3b)
circuit board: 9.5cm x 10cm
breadboards: 1

parts:
  ESP = ESP8266 WiFi Module [part_number=ESP8266]
  DRIVER1 = L293D [package=THT]
  DRIVER2 = L293D [package=THT]
  RELAY2 = OMRON PCB Power Relay – G5LE [part_number="G5LE-1\n" package=THT]
  RELAY3 = OMRON PCB Power Relay – G5LE [part_number="G5LE-1\n" package=THT]
  RELAY1 = OMRON PCB Power Relay – G5LE [part_number="G5LE-1\n" package=THT]
  OUT1 = screw terminal, 3 pins
  OUT3 = screw terminal, 3 pins
  OUT2 = screw terminal, 3 pins
  IN = screw terminal, 2 pins
  LM317 = Voltage Regulator [package=to220-adj]
  R1 = Resistor [tolerance=±5% resistance=220 package=THT]
  R2 = Resistor [tolerance=±5% resistance=220 package=THT]
  D1 = Rectifier Diode [part_number=1N4001 package="300 mil [THT]"]
  D2 = Rectifier Diode [part_number=1N4001 package="300 mil [THT]"]
  SW = Toggle Switch [package=THT]
  FUSE = female pin header, 2 pins [form="♀ (female)"]
  S = Toggle Switch [package=THT]
  ESP_2 = ESP8266 WiFi Module [part_number=ESP8266]
  DRIVER1_2 = L293D [package=THT]
  DRIVER2_2 = L293D [package=THT]
  RELAY2_2 = OMRON PCB Power Relay – G5LE [part_number="G5LE-1\n" package=THT]
  RELAY3_2 = OMRON PCB Power Relay – G5LE [part_number="G5LE-1\n" package=THT]
  RELAY1_2 = OMRON PCB Power Relay – G5LE [part_number="G5LE-1\n" package=THT]
  OUT3_2 = screw terminal, 3 pins
  OUT1_2 = screw terminal, 3 pins
  OUT2_2 = screw terminal, 3 pins
  IN_2 = screw terminal, 2 pins
  LM317_2 = Voltage Regulator [package=to220-adj]
  R3 = Resistor [tolerance=±5% resistance=220 package=THT]
  R4 = Resistor [tolerance=±5% resistance=220 package=THT]
  D3 = Rectifier Diode [part_number=1N4001 package="300 mil [THT]"]
  D4 = Rectifier Diode [part_number=1N4001 package="300 mil [THT]"]
  SW1 = Toggle Switch [package=THT]
  FUSE1 = female pin header, 2 pins [form="♀ (female)"]
  S1 = Toggle Switch [package=THT]

nets:
  N1: ESP.RXD, DRIVER1.In_1
  N2: ESP.VCC, ESP.CH_PD, LM317.ADJ, R1.Pin_0, R2.Pin_1, S.L2
  N3: ESP.GPIO_0, DRIVER2.In_1
  N4: ESP.GPIO_2, S.COM
  N5: ESP.GND, DRIVER1.0V, DRIVER2.0V, RELAY2.COIL2, RELAY3.COIL2, RELAY1.COIL2, R2.Pin_0, D1.anode, D2.anode, SW.COM, SW.L2, S.L1
  N6: ESP.TXD, DRIVER1.In_3
  N7: DRIVER1.Enable_1, DRIVER1.+Vmotor, DRIVER1.Enable_2, DRIVER1.+V, DRIVER2.Enable_1, DRIVER2.+Vmotor, DRIVER2.Enable_2, DRIVER2.+V, LM317.IN, D1.cathode, D2.cathode, FUSE.pin2
  N8: DRIVER1.Out_1_(_Controlled_by_Enable_1_), RELAY1.COIL1
  N9: DRIVER1.Out_3_(_Controlled_by_Enable_2_), RELAY2.COIL1
  N10: DRIVER2.Out_1_(_Controlled_by_Enable_1_), RELAY3.COIL1
  N11: RELAY2.A, OUT2.pin3
  N12: RELAY2.C, OUT2.pin2
  N13: RELAY2.B, OUT2.pin1
  N14: RELAY3.A, OUT3.pin3
  N15: RELAY3.C, OUT3.pin2
  N16: RELAY3.B, OUT3.pin1
  N17: RELAY1.A, OUT1.pin3
  N18: RELAY1.C, OUT1.pin2
  N19: RELAY1.B, OUT1.pin1
  N20: IN.pin1, FUSE.pin1
  N21: IN.pin2, SW.L1
  N22: LM317.OUT, R1.Pin_1
  N23: ESP_2.VCC, ESP_2.CH_PD, LM317_2.ADJ, R3.Pin_1, R4.Pin_0, S1.L2
  N24: ESP_2.GPIO_0, DRIVER2_2.In_1
  N25: ESP_2.GPIO_2, S1.COM
  N26: ESP_2.GND, DRIVER1_2.0V, DRIVER2_2.0V, RELAY2_2.COIL2, RELAY3_2.COIL2, RELAY1_2.COIL2, R3.Pin_0, D3.anode, D4.anode, SW1.COM, SW1.L2, S1.L1
  N27: ESP_2.TXD, DRIVER1_2.In_3
  N28: DRIVER1_2.Enable_1, DRIVER1_2.+Vmotor, DRIVER1_2.Enable_2, DRIVER1_2.+V, DRIVER2_2.Enable_1, DRIVER2_2.+Vmotor, DRIVER2_2.Enable_2, DRIVER2_2.+V, LM317_2.IN, D3.cathode, D4.cathode, FUSE1.pin2
  N29: DRIVER1_2.Out_3_(_Controlled_by_Enable_2_), RELAY2_2.COIL1
  N30: DRIVER2_2.Out_1_(_Controlled_by_Enable_1_), RELAY3_2.COIL1
  N31: RELAY2_2.A, OUT2_2.pin3
  N32: RELAY2_2.C, OUT2_2.pin2
  N33: RELAY2_2.B, OUT2_2.pin1
  N34: RELAY3_2.A, OUT3_2.pin3
  N35: RELAY3_2.C, OUT3_2.pin2
  N36: RELAY3_2.B, OUT3_2.pin1
  N37: RELAY1_2.A, OUT1_2.pin3
  N38: RELAY1_2.C, OUT1_2.pin2
  N39: RELAY1_2.B, OUT1_2.pin1
  N40: IN_2.pin1, FUSE1.pin1
  N41: IN_2.pin2, SW1.L1
  N42: LM317_2.OUT, R4.Pin_1

notes:
  IN+
  IN-
  -
  +
  IO2
  MADE IN EGYPT
  DP COMPANY CO.
  DP S01

custom parts:
  ESP8266 WiFi Module: Generic WiFi Module based on the ESP8266 with onboard PCB antenna and UART communications
